// Logisim project FelipeRezende.circ as structural Verilog
module Meio_Somador (
  input  A,
  input  B,
  output S,
  output S_2
);

  xor xor_1 (S, A, B);
  and and_1 (S_2, A, B);
endmodule

module Somador_completo (
  input  A,
  input  B,
  input  Te,
  output S,
  output S_2
);

  wire and_1_out, and_2_out, and_3_out, xor_1_out;

  xor xor_1 (xor_1_out, A, B);
  and and_1 (and_1_out, B, Te);
  and and_2 (and_2_out, B, A);
  and and_3 (and_3_out, B, A);
  xor xor_2 (S, xor_1_out, Te);
  or or_1 (S_2, and_1_out, and_2_out, and_3_out);
endmodule

module Somador_4bits (
  input  [3:0] A,
  input  [3:0] B,
  output [3:0] S,
  output C
);

  wire _1_2_s_2, Com_2_s_2, Com_s_2;

  Meio_Somador _1_2 (.A(A[0]), .B(B[0]), .S(S[0]), .S_2(_1_2_s_2));
  Somador_completo Com (.A(A[1]), .B(B[1]), .Te(_1_2_s_2), .S(S[1]), .S_2(Com_s_2));
  Somador_completo Com_2 (.A(A[2]), .B(B[2]), .Te(Com_s_2), .S(S[2]), .S_2(Com_2_s_2));
  Somador_completo Com_3 (.A(A[3]), .B(B[3]), .Te(Com_2_s_2), .S(S[3]), .S_2(C));
endmodule
